# Fritzing sketch connections (saved by Fritzing 0.9.2b)
circuit board: 8.46667cm x 5.64444cm

parts:
  U2 = NodeMCU V1.0
  J1 = ATX24 Pin Power Supply Connector [package=atx24_right_angle]
  U3 = 74HC595 [package="DIP16 [THT]"]
  Q1 = Basic FET N-Channel [package="TO220 [THT]"]
  LED1 = LED - 5mm [color="White (6500K)" package="5 mm [THT]"]

nets:
  GND: U2.D1, U2.D2, U2.GND, U2.RST, J1.GND, J1.PS_ON, U3.GND, U3.OE, Q1.source
  N1: U2.D3, J1.PWR_OK
  N2: U2.D5, U3.SH_CP
  N3: U2.D7, U3.DS
  N4: U2.D8, U3.ST_CP
  VIN: U2.Vin, J1.5V_STDBY, J1.12V, LED1.anode
  3.3V: J1.3.3V, U3.MR, U3.VCC
  N5: U3.Q1, Q1.gate
  N6: Q1.drain, LED1.cathode

custom parts:
  NodeMCU V1.0: ESP8266 based NodeMCU
